# Fritzing sketch PCB (saved by Fritzing 0.9.2b)
perfboards: 2

parts:
  J2 = male pin header, 3 pins [form="♂ (male)"]
  J5 = female pin header, 15 pins [form="♀ (female)"]
  J6 = female pin header, 15 pins [form="♀ (female)"]
  J7 = double row male pin header, 16 pins [form="♂ (male)"]
  J8 = double row male pin header, 16 pins [form="♂ (male)"]
  J1 = male pin header, 3 pins [form="♂ (male)"]
  J9 = male pin header, 3 pins [form="♂ (male)"]
  J10 = male pin header, 3 pins [form="♂ (male)"]
  J11 = male pin header, 4 pins [form="♂ (male)"]
  J12 = male pin header, 2 pins [form="♂ (male)"]
  Composant2 = Arduino Nano (Rev3.0) (ICSP)  # not connected
  S1 = Toggle Switch [package=THT]
  S2 = Toggle Switch [package=THT]
  J13 = male pin header, 2 pins [form="♂ (male)"]
  J4 = female pin header, 4 pins [form="♀ (female)"]

nets:
  N1: J2.pin1, J6.pin12, J1.pin1, J4.pin1
  N2: J2.pin2, J5.pin12, J1.pin2, J4.pin4
  N3: J2.pin3, J5.pin7
  N4: J5.pin5, J4.pin2, J4.pin3
  N5: J5.pin9, J1.pin3
  N6: J6.pin14, J13.pin1
  N7: J6.pin15, S2.COM
  N8: J7.pin6, J11.pin2, J11.pin3
  N9: J7.pin8, J10.pin3
  N10: J7.pin10, J9.pin3
  N11: J7.pin13, J9.pin2, J10.pin2, J11.pin1
  N12: J8.pin13, J9.pin1, J10.pin1, J11.pin4
  N13: J8.pin15, J12.pin1
  N14: J8.pin16, S1.L2
  N15: J12.pin2, S1.COM
  N16: S2.L2, J13.pin2

notes:
  Vu de dessus
  Vu de dessous
